# Fritzing sketch ParticleMind (saved by Fritzing 0.9.3b)
breadboards: 1

parts:
  Part1 = Adafruit Feather nRF52 [part_number="Adafruit #3406"]
  Red = Pushbutton [package="[THT]"]
  Green = Pushbutton [package="[THT]"]
  NEOPIXEL1 = Neopixel Strip -- Black (60/m)
  Part2 = Adafruit Breadboard-Friendly NeoPixel [part_number="Adafruit #1312"]
  Diode = Rectifier Diode [part_number=(O/B) package="300 mil [THT]"]
  LED1 = LED - 3mm [color="Red (633nm)" package="3 mm [THT]"]
  LED2 = LED - 3mm [color="Green (555nm)" package="3 mm [THT]"]
  R1 = Resistor [tolerance=±5% resistance=220 package="0603 [SMD]"]
  R2 = Resistor [tolerance=±5% resistance=220 package="0603 [SMD]"]

nets:
  GND: Part1.GND, Part1.MISO, Part1.RXD, Red.Pin_1, Red.Pin_2, Red.Pin_3, Red.Pin_4, Green.Pin_1, Green.Pin_2, Green.Pin_3, Green.Pin_4, NEOPIXEL1.GND, Part2.GND, R1.Pin_0, R2.Pin_0
  N1: Part1.P0.27, Part2.IN
  N2: Part1.A7/P0.31, LED1.anode
  N3: Part1.P0.07, LED2.anode
  N4: Part1.VBUS, NEOPIXEL1.+5V, Diode.anode
  N5: NEOPIXEL1.DI, Part2.OUT
  N6: Part2.VDD, Diode.cathode
  N7: LED1.cathode, R2.Pin_1
  N8: LED2.cathode, R1.Pin_1

custom parts:
  Neopixel Strip -- Black (60/m): Neopixel Strip, Black, 60 pixels per meter.
  Adafruit Breadboard-Friendly NeoPixel: This is the easiest way possible to add small, bright RGB pixels to your project. We took the same technology from our Flora NeoPixels and made them breadboard friendly, with two rows of 3 x 0.1" spaced header on each side for easy soldering, chaining and breadboarding. These ultra-bright LEDs have a constant-current driver cooked right into the LED package! The pixels are chainable - so you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
